// Logisim project 6651071093_LAB1_bai2.circ as structural Verilog: 1 circuit, main circuit main
module main (
  input  A,
  input  B,
  input  C,
  output Y
);

  wire xor_1_out;

  xor xor_1 (xor_1_out, A, B);
  and and_1 (Y, xor_1_out, C);

  // Notes on the sheet:
  //   Trần Ngọc Minh Vũ_6651071093
endmodule
