// Logisim project TranNgocMinhVu_6651071093_Bai3.circ as structural Verilog: 2 circuits, main circuit main
module main (
  input  [3:0] Data_3_0,
  output [3:0] Q_3_0
);

  wire clock_1_out;

  Clock clock_1 (.out(clock_1_out));
  Register #(.width(4)) register_1 (.D(Data_3_0), .en(1'b1), .Q(Q_3_0), .clk(clock_1_out), .clr(1'b0));
endmodule

module BCT_3a (
  input  E,
  input  D,
  output Q
);

  wire and_1_out, and_2_out, not_1_out, not_2_out;

  not not_1 (not_1_out, E);
  not not_2 (not_2_out, D);
  and and_1 (and_1_out, not_1_out, not_2_out);
  and and_2 (and_2_out, E, D);
  or or_1 (Q, and_1_out, and_2_out);
endmodule
