// Logisim project TranNgocMinhVu_6651071093_Bai4.circ as structural Verilog: 2 circuits, main circuit main
module main (
  input  A,
  input  B,
  input  C,
  output F
);

  wire and_1_out;

  and and_1 (and_1_out, A, B);
  or or_1 (F, and_1_out, C);
endmodule

module BCT_Cau4 (
  input  A,
  input  B,
  input  C,
  output F
);

  wire and_1_out;

  and and_1 (and_1_out, A, B);
  or or_1 (F, C, and_1_out);
endmodule
