// Logisim project TranNgocMinhVu_6651071093_Bai5.circ as structural Verilog: 1 circuit, main circuit main
module main (
  input  D3,
  input  D2,
  input  D1,
  input  D0,
  output Q3,
  output Q2,
  output Q1,
  output Q0
);

  wire clock_1_out;
  wire [3:0] register_1_q;

  Clock clock_1 (.out(clock_1_out));
  Register #(.width(4)) register_1 (.D({D3, D2, D1, D0}), .en(1'b1), .Q(register_1_q), .clk(clock_1_out), .clr(1'b0));
  Adder #(.width(4)) adder_1 (.a(4'b0010), .b(register_1_q), .out({Q3, Q2, Q1, Q0}));  // open: cin, cout
endmodule
